// Logisim project 333.circ as structural Verilog: 1 circuit, main circuit main
module main (
  input  X,
  input  Y,
  output out_3
);

  wire or_1_out, or_2_out;

  or or_1 (or_1_out, X, Y);
  or or_2 (or_2_out, Y, X);
  and and_1 (out_3, or_1_out, or_2_out);

  // Notes on the sheet:
  //   X+Y
  //   X+Y
  //   (X+Y)(X+Y)
endmodule
