// Logisim project 444.circ as structural Verilog: 1 circuit, main circuit main
module main (
  input  x,
  input  y,
  input  z,
  input  w,
  output out_5
);

  wire and_1_out, and_2_out, and_3_out, or_1_out;

  and and_1 (and_1_out, w, z);
  and and_2 (and_2_out, z, w);
  and and_3 (and_3_out, x, y);
  or or_1 (or_1_out, and_1_out, and_2_out);
  or or_2 (out_5, and_3_out, or_1_out);

  // Notes on the sheet:
  //   wz
  //   wz
  //   xy
  //   wz+wz
  //   xy+x(wz+wz)
endmodule
