// Logisim project Lab1.2_CircuitF3.circ as structural Verilog: 1 circuit, main circuit main
module main (
  input  x,
  input  y,
  input  z,
  output out_4
);

  wire and_1_out, and_2_out, not_1_out, not_2_out;

  not not_1 (not_1_out, y);
  not not_2 (not_2_out, z);
  and and_1 (and_1_out, x, not_1_out);
  and and_2 (and_2_out, not_2_out, x);
  or or_1 (out_4, and_1_out, and_2_out);

  // Notes on the sheet:
  //   x.y'
  //   x.z'
  //   x.y'+x.z'
endmodule
