// Logisim project what.circ as structural Verilog: 1 circuit, main circuit main
module main (
  input  X,
  input  Y,
  input  Z,
  output out_4
);

  wire and_1_out, and_2_out;

  and and_1 (and_1_out, X, Y, Z);
  and and_2 (and_2_out, X, X, Z);
  or or_1 (out_4, and_1_out, and_2_out);

  // Notes on the sheet:
  //   XYZ
  //   XZ
  //   XYZ+XZ
endmodule
