// Logisim project lab21.circ as structural Verilog: 2 circuits, main circuit HALFADDER
module HALFADDER (
  input  A,
  input  B,
  output S,
  output Cout
);

  wire and_2_out, and_3_out, not_1_out, not_2_out;

  not not_1 (not_1_out, A);
  not not_2 (not_2_out, B);
  and and_1 (Cout, A, B);
  and and_2 (and_2_out, not_1_out, B);
  and and_3 (and_3_out, A, not_2_out);
  or or_1 (S, and_2_out, and_3_out);
endmodule

module main (
  input  A,
  input  B,
  input  C,
  output S,
  output Cout
);

  wire halfadder_1_cout, halfadder_1_s, halfadder_2_cout;

  HALFADDER halfadder_1 (.A(A), .B(B), .S(halfadder_1_s), .Cout(halfadder_1_cout));
  HALFADDER halfadder_2 (.A(halfadder_1_s), .B(C), .S(S), .Cout(halfadder_2_cout));
  or or_1 (Cout, halfadder_1_cout, halfadder_2_cout);
endmodule
