// Logisim project lab22.circ as structural Verilog: 2 circuits, main circuit main
module main (
  input  [3:0] in_1,
  input  [3:0] in_2,
  input  in_3,
  output out_4,
  output [3:0] out_5
);

  wire n1_bit_adder_1_s, n1_bit_adder_2_s, n1_bit_adder_3_s;

  _1_bit_adder u_1_bit_adder_1 (.A(in_1[0]), .B(in_2[3]), .Cin(in_2[3]), .Cout(out_5[0]), .S(n1_bit_adder_1_s));
  _1_bit_adder u_1_bit_adder_2 (
    .A(in_1[1]), .B(in_2[1]), .Cin(n1_bit_adder_1_s), .Cout(out_5[1]), .S(n1_bit_adder_2_s));
  _1_bit_adder u_1_bit_adder_3 (
    .A(in_1[2]), .B(in_2[2]), .Cin(n1_bit_adder_2_s), .Cout(out_5[2]), .S(n1_bit_adder_3_s));
  _1_bit_adder u_1_bit_adder_4 (.A(in_1[3]), .B(in_2[0]), .Cin(n1_bit_adder_3_s), .Cout(out_5[3]), .S(out_4));

  assign in_3 = in_2[3];
endmodule

module _1_bit_adder (
  input  A,
  input  B,
  input  Cin,
  output Cout,
  output S
);

  wire and_1_out, and_2_out, and_3_out, and_4_out, and_5_out, and_6_out, and_7_out, not_1_out, not_2_out,
       not_3_out, not_4_out, not_5_out, not_6_out;

  and and_1 (and_1_out, B, Cin);
  and and_2 (and_2_out, A, Cin);
  and and_3 (and_3_out, A, B);
  not not_1 (not_1_out, A);
  not not_2 (not_2_out, B);
  not not_3 (not_3_out, A);
  not not_4 (not_4_out, Cin);
  not not_5 (not_5_out, B);
  not not_6 (not_6_out, Cin);
  or or_1 (Cout, and_1_out, and_2_out, and_3_out);
  and and_4 (and_4_out, not_1_out, not_2_out, Cin);
  and and_5 (and_5_out, not_3_out, B, not_4_out);
  and and_6 (and_6_out, A, not_5_out, not_6_out);
  and and_7 (and_7_out, A, B, Cin);
  or or_2 (S, and_4_out, and_5_out, and_6_out, and_7_out);
endmodule
